# Fritzing sketch relaysak (saved by Fritzing 0.9.3b)
circuit board: 7.29156cm x 5.7145cm
breadboards: 1

parts:
  Relay_for_Pro_Micro = SparkFun Pro Micro [part_number=DEV-12640]
  OneWire = screw terminal, 3 pins
  I2C_OLED = screw terminal, 4 pins
  J6 = Screw terminal - 2 pins [package=THT]
  J8 = Screw terminal - 2 pins [package=THT]
  J11 = Screw terminal - 2 pins [package=THT]
  UP = Pushbutton [package="[THT]"]
  SEL = Pushbutton [package="[THT]"]
  DWN = Pushbutton [package="[THT]"]
  R1 = Resistor [tolerance=±5% resistance=220 package=THT]
  R2 = Resistor [tolerance=±5% resistance=220 package=THT]
  R3 = Resistor [tolerance=±5% resistance=220 package=THT]
  RST = Pushbutton [package="[THT]"]
  OneWire1 = screw terminal, 6 pins
  R4 = Resistor [tolerance=±5% resistance=220 package=THT]
  U4 = RELAY-SOLIDSTATE [package=relay-s108t02]
  U5 = RELAY-SOLIDSTATE [package=relay-s108t02]
  U6 = RELAY-SOLIDSTATE [package=relay-s108t02]

nets:
  N1: Relay_for_Pro_Micro.GND, OneWire.pin2, I2C_OLED.pin2, R1.Pin_0, R2.Pin_0, R3.Pin_0, RST.Pin_1, RST.Pin_2, OneWire1.pin6, U4.-, U5.-, U6.-
  N2: Relay_for_Pro_Micro.RESET, RST.Pin_3, RST.Pin_4
  N3: Relay_for_Pro_Micro.VCC, OneWire.pin3, I2C_OLED.pin1, UP.Pin_1, UP.Pin_2, SEL.Pin_1, SEL.Pin_2, DWN.Pin_1, DWN.Pin_2, OneWire1.pin5, R4.Pin_1
  N4: Relay_for_Pro_Micro.A3, OneWire1.pin1
  N5: Relay_for_Pro_Micro.A2, SEL.Pin_3, SEL.Pin_4, R3.Pin_1
  N6: Relay_for_Pro_Micro.A1, DWN.Pin_3, DWN.Pin_4, R1.Pin_1
  N7: Relay_for_Pro_Micro.A0, UP.Pin_3, UP.Pin_4, R2.Pin_1
  N8: Relay_for_Pro_Micro.D10, OneWire1.pin4
  N9: Relay_for_Pro_Micro.D9, OneWire1.pin2
  N10: Relay_for_Pro_Micro.D8, OneWire.pin1, R4.Pin_0
  N11: Relay_for_Pro_Micro.D7, U6.+
  N12: Relay_for_Pro_Micro.D6, U5.+
  N13: Relay_for_Pro_Micro.D5, U4.+
  N14: Relay_for_Pro_Micro.D4, OneWire1.pin3
  N15: Relay_for_Pro_Micro.D3, I2C_OLED.pin3
  N16: Relay_for_Pro_Micro.D2, I2C_OLED.pin4
  N17: J6.pin1, U4.T1
  N18: J6.pin2, U4.T2
  N19: J8.pin1, U6.T1
  N20: J8.pin2, U6.T2
  N21: J11.pin1, U5.T1
  N22: J11.pin2, U5.T2

notes:
  +
  2019
  Bogg

custom parts:
  SparkFun Pro Micro: This tiny little board does all of the neat-o Arduino tricks that you’re familiar with: 4 channels of 10-bit ADC, 5 PWM pins, 12 DIOs as well as hardware serial connections Rx and Tx. Running at 16MHz and 5V, this board will remind you a lot of your other favorite Arduino-compatible boards but this little guy can go just about anywhere. There is a voltage regulator on board so it can accept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
